# Fritzing sketch cable-continuity-tester (saved by Fritzing 1.0.7)
# 18650 Li-ion Battery: CC-BY Dr Kristofer Chan, King's College London/Remote-research.org

parts:
  BAT1 = 18650 Li-ion Battery [package=battery-18650]
  TP1 = TP4056 [chip_label=TP4056 package="DIP (Dual Inline) [THT]"]
  S4 = SWITCH-SPST-2 [package=switch-spst-vertical]
  LED1 = LED - 5mm [color="Green (555nm)" current=0.030A package="5 mm [THT]"]
  R1 = Resistor [tolerance=±5% resistance=1k package="2512 [SMD]"]
  R2 = Resistor [tolerance=±5% resistance=100 package="2512 [SMD]"]
  R4 = Rotary Potentiometer (Small) [maximum_resistance=10kΩ knob_status=50% power=0.5W package=THT]
  JACK1 = 2.1mm DC Barrel Jack
  Test_Leads = 2.1mm DC Barrel Jack
  J2 = Piezo Speaker

nets:
  N1: BAT1.-, TP1.pin5
  N2: BAT1.+, TP1.pin4
  N3: TP1.pin3, S4.O
  N4: TP1.pin6, LED1.cathode, R2.Pin_0, JACK1.sleeve, J2.pin1
  N5: S4.P, JACK1.center, Test_Leads.center
  N6: LED1.anode, R1.Pin_0
  N7: R1.Pin_1, R4.leg2, Test_Leads.sleeve
  N8: R2.Pin_1, R4.leg1
  N9: R4.wiper, J2.pin2

custom parts:
  18650 Li-ion Battery: 18650 li-ion Battery Standard 18650 battery with interactive connectors Creative Common Attribution 4.0 International (CC-BY 4.0) license. Any use of this part requires attribution of Dr Kristofer Chan, Department of Geography, King's College London. Contact kristofer.chan [at] kcl.ac.uk OR kris [at] remote-research.org for further information.
  TP4056: A DIP stand-in part for whatever IC you want. With 6 pins on a 300mil dual inline package (DIP) footprint.
